# Fritzing sketch wiring_diagram (saved by Fritzing 0.9.6b)
breadboards: 1

parts:
  J1 = Basic Servo
  S1 = Round Pushbutton
  part = Real Time Clock Module - DS1307 RTC Breakout Board [part_number="RTC module"]
  R1 = Resistor [tolerance=±1% power=0pW resistance=2 package=THT]
  Microcontroller = Arduino Nano 33 IOT
  C1 = Electrolytic Capacitor [capacitance=0.47mF voltage=35V package="0807 [SMD, electrolytic]"]

nets:
  GND: J1.gnd, S1.leg0, part.GND, Microcontroller.GND, Microcontroller.D13~
  N1: J1.vcc, R1.Pin_1
  N2: J1.pulse, Microcontroller.D3~
  N3: S1.leg1, Microcontroller.D6~
  5V: part.5V, R1.Pin_0, Microcontroller.D11/MOSI, Microcontroller.+5V
  N4: part.SCL, Microcontroller.A5
  N5: part.SDA, Microcontroller.A4
  GND_2: C1.-

custom parts:
  Arduino Nano 33 IOT: The Arduino Nano 33 IoT is the easiest and cheapest point of entry to enhance existing devices (and creating new ones) to be part of the IoT and designing pico-network applications. Whether you are looking at building a sensor network connected to your office or home router, or if you want to create a BLE device sending data to a cellphone, the Nano 33 IoT is your one-stop-solution for many of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
